// Digital circuit and.dig as structural Verilog
module \and  (
);

  Switch #(.switchActsAsInput("true")) switch_0 ();  // open: A, B
  Switch #(.switchActsAsInput("true")) switch_1 ();  // open: A, B
  // PolarityAwareLED LED: pin names not known; wires that end beside it: 1'b1, 1'b0
endmodule

/* Test case:
switch_0 switch_1 LED
0 0 Z
0 1 Z
1 0 Z
1 1 1
*/
